# Fritzing sketch esp32.with.pir (saved by Fritzing 0.9.4)
breadboards: 1

parts:
  U2 = ESP32-38PinWide [part_number=ESP32-38PinWide]
  PIR1 = PIR sensor

nets:
  GND: U2.GND, PIR1.GND
  N1: U2.GPIO13, PIR1.SIG
  VIN: U2.VIN, PIR1.VDD

custom parts:
  ESP32-38PinWide: Generic 38-Pin ESP32 with wide format (only access to one side of pins on a breadboard) based on Stephen Lilley's HiLetgo ESP-WROOM-32 ESP32 ESP-32S Development Board.
